// Logisim project F3.circ as structural Verilog: 37 circuits, main circuit my_xor
module my_xor (
  input  in_1,
  input  in_2,
  output out_3
);

  wire and_1_out, nor_1_out;

  nor nor_1 (nor_1_out, in_1, in_2);
  and and_1 (and_1_out, in_1, in_2);
  nor nor_2 (out_3, nor_1_out, and_1_out);
endmodule

module my_xnor (
  input  in_1,
  input  in_2,
  output out_3
);

  wire nand_1_out, or_1_out;

  or or_1 (or_1_out, in_1, in_2);
  nand nand_1 (nand_1_out, in_1, in_2);
  nand nand_2 (out_3, nand_1_out, or_1_out);
endmodule

module my_2_4_decoder (
  input  A0,
  input  A1,
  output Y0,
  output Y1,
  output Y2,
  output Y3
);

  wire not_1_out, not_2_out;

  not not_1 (not_1_out, A0);
  not not_2 (not_2_out, A1);
  and and_1 (Y0, not_1_out, not_2_out);
  and and_2 (Y1, A0, not_2_out);
  and and_3 (Y2, not_1_out, A1);
  and and_4 (Y3, A0, A1);
endmodule

module my_3_8_decoder (
  input  A0,
  input  A1,
  input  A2,
  output Y0,
  output Y1,
  output Y2,
  output Y3,
  output Y4,
  output Y5,
  output Y6,
  output Y7
);

  wire [3:0] my_2_4_decoder_1_y0, my_2_4_decoder_2_y0, not_1_out;

  my_2_4_decoder my_2_4_decoder_1 (
    .A0(A0), .A1(A1), .Y0(my_2_4_decoder_1_y0[0]), .Y1(my_2_4_decoder_1_y0[1]), .Y2(my_2_4_decoder_1_y0[2]),
    .Y3(my_2_4_decoder_1_y0[3]));
  my_2_4_decoder my_2_4_decoder_2 (
    .A0(A0), .A1(A1), .Y0(my_2_4_decoder_2_y0[0]), .Y1(my_2_4_decoder_2_y0[1]), .Y2(my_2_4_decoder_2_y0[2]),
    .Y3(my_2_4_decoder_2_y0[3]));
  assign not_1_out = ~{4{A2}};  // NOT_Gate not_1, 4 bits wide
  assign {Y3, Y2, Y1, Y0} = my_2_4_decoder_1_y0 & not_1_out;  // AND_Gate and_1, 4 bits wide
  assign {Y7, Y6, Y5, Y4} = my_2_4_decoder_2_y0 & {4{A2}};  // AND_Gate and_2, 4 bits wide
endmodule

module my_decoder_segment (
  input  [3:0] in_1
);

  wire decoder_1_out0, decoder_1_out1, decoder_1_out2, decoder_1_out3, decoder_1_out4, decoder_1_out5,
       decoder_1_out6, decoder_1_out7, decoder_1_out8, decoder_1_out9, decoder_1_out10, decoder_1_out11,
       decoder_1_out12, decoder_1_out13, decoder_1_out14, decoder_1_out15, nor_1_out, nor_2_out, nor_3_out,
       nor_4_out, nor_5_out, nor_6_out, nor_7_out;

  Decoder #(.select(4)) decoder_1 (
    .out0(decoder_1_out0), .out1(decoder_1_out1), .out2(decoder_1_out2), .out3(decoder_1_out3),
    .out4(decoder_1_out4), .out5(decoder_1_out5), .out6(decoder_1_out6), .out7(decoder_1_out7),
    .out8(decoder_1_out8), .out9(decoder_1_out9), .out10(decoder_1_out10), .out11(decoder_1_out11),
    .out12(decoder_1_out12), .out13(decoder_1_out13), .out14(decoder_1_out14), .out15(decoder_1_out15),
    .sel(in_1));  // open: en
  nor nor_1 (nor_1_out, decoder_1_out1, decoder_1_out4, decoder_1_out7, decoder_1_out10, decoder_1_out15);
  nor nor_2 (nor_2_out, decoder_1_out2, decoder_1_out12, decoder_1_out14, decoder_1_out15);
  nor nor_3 (nor_3_out, decoder_1_out1, decoder_1_out3, decoder_1_out4, decoder_1_out5, decoder_1_out7, decoder_1_out9);
  nor nor_4 (nor_4_out, decoder_1_out5, decoder_1_out6, decoder_1_out11, decoder_1_out12, decoder_1_out14, decoder_1_out15);
  nor nor_5 (nor_5_out, decoder_1_out1, decoder_1_out2, decoder_1_out3, decoder_1_out7, decoder_1_out13);
  nor nor_6 (nor_6_out, decoder_1_out1, decoder_1_out4, decoder_1_out11, decoder_1_out13);
  nor nor_7 (nor_7_out, decoder_1_out0, decoder_1_out1, decoder_1_out7, decoder_1_out12);
  _7_Segment_Display u_7_segment_display_1 (
    .g(nor_7_out), .f(nor_5_out), .a(nor_6_out), .b(nor_4_out), .e(nor_3_out), .d(nor_1_out), .c(nor_2_out));  // open: dp
endmodule

module my_encoder_segment (
  input  [3:0] in_1
);

  wire decoder_1_out0, decoder_1_out1, decoder_1_out2, decoder_1_out3, decoder_1_out4, decoder_1_out5,
       decoder_1_out6, decoder_1_out7, decoder_1_out8, decoder_1_out9, decoder_1_out10, decoder_1_out11,
       decoder_1_out12, decoder_1_out13, decoder_1_out14, decoder_1_out15, nor_1_out, nor_2_out, nor_3_out,
       nor_4_out, nor_5_out, nor_6_out, nor_7_out;

  Decoder #(.select(4)) decoder_1 (
    .out0(decoder_1_out0), .out1(decoder_1_out1), .out2(decoder_1_out2), .out3(decoder_1_out3),
    .out4(decoder_1_out4), .out5(decoder_1_out5), .out6(decoder_1_out6), .out7(decoder_1_out7),
    .out8(decoder_1_out8), .out9(decoder_1_out9), .out10(decoder_1_out10), .out11(decoder_1_out11),
    .out12(decoder_1_out12), .out13(decoder_1_out13), .out14(decoder_1_out14), .out15(decoder_1_out15),
    .sel(in_1));  // open: en
  nor nor_1 (nor_1_out, decoder_1_out1, decoder_1_out4, decoder_1_out7, decoder_1_out10, decoder_1_out15);
  nor nor_2 (nor_2_out, decoder_1_out2, decoder_1_out12, decoder_1_out14, decoder_1_out15);
  nor nor_3 (nor_3_out, decoder_1_out1, decoder_1_out3, decoder_1_out4, decoder_1_out5, decoder_1_out7, decoder_1_out9);
  nor nor_4 (nor_4_out, decoder_1_out5, decoder_1_out6, decoder_1_out11, decoder_1_out12, decoder_1_out14, decoder_1_out15);
  nor nor_5 (nor_5_out, decoder_1_out1, decoder_1_out2, decoder_1_out3, decoder_1_out7, decoder_1_out13);
  nor nor_6 (nor_6_out, decoder_1_out1, decoder_1_out4, decoder_1_out11, decoder_1_out13);
  nor nor_7 (nor_7_out, decoder_1_out0, decoder_1_out1, decoder_1_out7, decoder_1_out12);
  _7_Segment_Display u_7_segment_display_1 (
    .g(nor_7_out), .f(nor_5_out), .a(nor_6_out), .b(nor_4_out), .e(nor_3_out), .d(nor_1_out), .c(nor_2_out));  // open: dp
endmodule

module my_16_4_encoder (
  input  [15:0] in_1
);

  wire [1:0] multiplexer_1_out, my_4_2_encoder_1_y, my_4_2_encoder_2_y, my_4_2_encoder_3_y,
       my_4_2_encoder_4_y, my_4_2_encoder_5_y;
  wire [3:0] my_4_2_encoder_1_valid;

  my_4_2_encoder my_4_2_encoder_1 (.X(in_1[3:0]), .Y(my_4_2_encoder_1_y), .Valid(my_4_2_encoder_1_valid[0]));
  my_4_2_encoder my_4_2_encoder_2 (.X(in_1[7:4]), .Y(my_4_2_encoder_2_y), .Valid(my_4_2_encoder_1_valid[1]));
  my_4_2_encoder my_4_2_encoder_3 (.X(in_1[11:8]), .Y(my_4_2_encoder_3_y), .Valid(my_4_2_encoder_1_valid[2]));
  my_4_2_encoder my_4_2_encoder_4 (.X(in_1[15:12]), .Y(my_4_2_encoder_4_y), .Valid(my_4_2_encoder_1_valid[3]));
  Multiplexer #(.select(2), .width(2)) multiplexer_1 (
    .in0(my_4_2_encoder_1_y), .in1(my_4_2_encoder_2_y), .in2(my_4_2_encoder_3_y), .in3(my_4_2_encoder_4_y),
    .out(multiplexer_1_out), .sel(my_4_2_encoder_5_y));
  my_4_2_encoder my_4_2_encoder_5 (.X(my_4_2_encoder_1_valid), .Y(my_4_2_encoder_5_y));  // open: Valid
  Hex_Digit_Display hex_digit_display_1 (.value({my_4_2_encoder_5_y, multiplexer_1_out}));  // open: dp
endmodule

module my_4_2_encoder (
  input  [3:0] X,
  output [1:0] Y,
  output Valid
);

  wire and_1_out;

  or or_1 (Y[1], X[3], X[2]);
  and and_1 (and_1_out, ~X[2], X[1]);  // AND_Gate
  or or_2 (Y[0], X[3], and_1_out);
  or or_3 (Valid, X[3], X[2], X[1], X[0]);
endmodule

module my_mux (
  input  S,
  input  D0,
  input  D1,
  output Y
);

  wire and_1_out, and_2_out, not_1_out;

  not not_1 (not_1_out, S);
  and and_1 (and_1_out, not_1_out, D0);
  and and_2 (and_2_out, S, D1);
  or or_1 (Y, and_1_out, and_2_out);
endmodule

module my_mux2 (
  input  S0,
  input  S1,
  input  D0,
  input  D1,
  input  D2,
  input  D3,
  output Y
);

  wire my_mux_1_y, my_mux_2_y;

  my_mux my_mux_1 (.S(S0), .D0(D0), .D1(D1), .Y(my_mux_1_y));
  my_mux my_mux_2 (.S(S0), .D0(D2), .D1(D3), .Y(my_mux_2_y));
  my_mux my_mux_3 (.S(S1), .D0(my_mux_1_y), .D1(my_mux_2_y), .Y(Y));
endmodule

module my_cmp (
  input  [3:0] in_1,
  input  [3:0] in_2,
  output out_3
);

  wire [3:0] xnor_1_out;

  assign xnor_1_out = ~(in_1 ^ in_2);  // XNOR_Gate xnor_1, 4 bits wide
  and and_1 (out_3, xnor_1_out[0], xnor_1_out[1], xnor_1_out[2], xnor_1_out[3]);
endmodule

module my_half_adder (
  input  A,
  input  B,
  output S,
  output C
);

  xor xor_1 (S, A, B);
  and and_1 (C, A, B);
endmodule

module my_adder (
  input  A,
  input  B,
  input  Cin,
  output S,
  output Cout
);

  wire and_1_out, and_2_out, and_3_out, xor_1_out;

  xor xor_1 (xor_1_out, A, B);
  and and_1 (and_1_out, A, B);
  and and_2 (and_2_out, A, Cin);
  and and_3 (and_3_out, B, Cin);
  xor xor_2 (S, xor_1_out, Cin);
  or or_1 (Cout, and_1_out, and_2_out, and_3_out);
endmodule

module my_adder2 (
  input  A,
  input  B,
  input  Cin,
  output S,
  output Cout
);

  wire my_half_adder_1_c, my_half_adder_1_s, my_half_adder_2_c;

  my_half_adder my_half_adder_1 (.A(A), .B(B), .S(my_half_adder_1_s), .C(my_half_adder_1_c));
  my_half_adder my_half_adder_2 (.A(my_half_adder_1_s), .B(Cin), .S(S), .C(my_half_adder_2_c));
  or or_1 (Cout, my_half_adder_2_c, my_half_adder_1_c);
endmodule

module my_adder4 (
  input  [3:0] A,
  input  [3:0] B,
  input  Cin,
  output [3:0] S,
  output Cout
);

  wire my_adder_1_cout, my_adder_2_cout, my_adder_3_cout;

  Hex_Digit_Display hex_digit_display_1 (.value(A));  // open: dp
  Hex_Digit_Display hex_digit_display_2 (.value(B));  // open: dp
  my_adder my_adder_1 (.A(A[0]), .B(B[0]), .Cin(Cin), .S(S[0]), .Cout(my_adder_1_cout));
  my_adder my_adder_2 (.A(A[1]), .B(B[1]), .Cin(my_adder_1_cout), .S(S[1]), .Cout(my_adder_2_cout));
  my_adder my_adder_3 (.A(A[2]), .B(B[2]), .Cin(my_adder_2_cout), .S(S[2]), .Cout(my_adder_3_cout));
  my_adder my_adder_4 (.A(A[3]), .B(B[3]), .Cin(my_adder_3_cout), .S(S[3]), .Cout(Cout));
  Hex_Digit_Display hex_digit_display_3 (.value(S));  // open: dp
  LED led_1 (.in(Cout));
endmodule

module my_sub (
  input  A,
  input  B,
  output S,
  output C
);

  xor xor_1 (S, A, B);
  and and_1 (C, ~A, B);  // AND_Gate
endmodule

module my_sub2 (
  input  A,
  input  B,
  input  Cin,
  output S,
  output Cout
);

  wire my_sub_1_c, my_sub_1_s, my_sub_2_c;

  my_sub my_sub_1 (.A(A), .B(B), .S(my_sub_1_s), .C(my_sub_1_c));
  my_sub my_sub_2 (.A(my_sub_1_s), .B(Cin), .S(S), .C(my_sub_2_c));
  or or_1 (Cout, my_sub_2_c, my_sub_1_c);
endmodule

module my_sub4 (
  input  [3:0] A,
  input  [3:0] B,
  input  Cin,
  output [3:0] S,
  output Cout
);

  wire my_sub2_1_cout, my_sub2_2_cout, my_sub2_3_cout;

  Hex_Digit_Display hex_digit_display_1 (.value(A));  // open: dp
  Hex_Digit_Display hex_digit_display_2 (.value(B));  // open: dp
  my_sub2 my_sub2_1 (.A(A[0]), .B(B[0]), .Cin(Cin), .S(S[0]), .Cout(my_sub2_1_cout));
  my_sub2 my_sub2_2 (.A(A[1]), .B(B[1]), .Cin(my_sub2_1_cout), .S(S[1]), .Cout(my_sub2_2_cout));
  my_sub2 my_sub2_3 (.A(A[2]), .B(B[2]), .Cin(my_sub2_2_cout), .S(S[2]), .Cout(my_sub2_3_cout));
  my_sub2 my_sub2_4 (.A(A[3]), .B(B[3]), .Cin(my_sub2_3_cout), .S(S[3]), .Cout(Cout));
  Hex_Digit_Display hex_digit_display_3 (.value(S));  // open: dp
  LED led_1 (.in(Cout));
endmodule

module my_true_adder (
  input  [4:0] in_1,
  input  [4:0] in_2,
  output [3:0] S,
  output Cout,
  output Sign
);

  wire and_2_out, and_3_out, my_adder4_1_cout, my_sub4_1_cout, not_1_out, xor_1_out, xor_2_out;
  wire [3:0] multiplexer_1_out, my_adder4_1_s, my_sub4_1_s, my_sub4_2_s;

  _7_Segment_Display u_7_segment_display_1 (.g(in_1[4]));  // open: f, a, b, e, d, c, dp
  _7_Segment_Display u_7_segment_display_2 (.g(in_2[4]));  // open: f, a, b, e, d, c, dp
  Hex_Digit_Display hex_digit_display_1 (.value(in_1[3:0]));  // open: dp
  Hex_Digit_Display hex_digit_display_2 (.value(in_2[3:0]));  // open: dp
  xor xor_1 (xor_1_out, in_1[4], in_2[4]);
  my_adder4 my_adder4_1 (.A(in_1[3:0]), .B(in_2[3:0]), .Cin(1'b0), .S(my_adder4_1_s), .Cout(my_adder4_1_cout));
  my_sub4 my_sub4_1 (.A(in_1[3:0]), .B(in_2[3:0]), .Cin(1'b0), .S(my_sub4_1_s), .Cout(my_sub4_1_cout));
  my_sub4 my_sub4_2 (.A(in_2[3:0]), .B(in_1[3:0]), .Cin(1'b0), .S(my_sub4_2_s));  // open: Cout
  // Probe on my_adder4_1_s
  // Probe on multiplexer_1_out
  Multiplexer #(.width(4)) multiplexer_1 (
    .in0(my_sub4_1_s), .in1(my_sub4_2_s), .out(multiplexer_1_out), .sel(my_sub4_1_cout));
  Multiplexer #(.width(4)) multiplexer_2 (.in0(my_adder4_1_s), .in1(multiplexer_1_out), .out(S), .sel(xor_1_out));
  xor xor_2 (xor_2_out, my_sub4_1_cout, in_1[4]);
  not not_1 (not_1_out, xor_1_out);
  _7_Segment_Display u_7_segment_display_3 (.g(Sign));  // open: f, a, b, e, d, c, dp
  Hex_Digit_Display hex_digit_display_3 (.value(S));  // open: dp
  and and_1 (Cout, my_adder4_1_cout, not_1_out);
  and and_2 (and_2_out, not_1_out, in_1[4]);
  and and_3 (and_3_out, xor_1_out, xor_2_out);
  or or_1 (Sign, and_2_out, and_3_out);
endmodule

module my_sr_reg (
  input  R,
  input  S,
  output Q,
  output Qn
);

  nor nor_1 (Q, R, Qn);
  nor nor_2 (Qn, Q, S);
endmodule

module my_sr_reg_n (
  input  R,
  input  S,
  output Q,
  output Qn
);

  nand nand_1 (Q, R, Qn);
  nand nand_2 (Qn, Q, S);
endmodule

module my_d_reg (
  input  WE,
  input  D,
  output Q,
  output Qn
);

  wire and_1_out, and_2_out, not_1_out;

  not not_1 (not_1_out, D);
  and and_1 (and_1_out, not_1_out, WE);
  and and_2 (and_2_out, WE, D);
  nor nor_1 (Q, and_1_out, Qn);
  nor nor_2 (Qn, Q, and_2_out);
endmodule

module my_d_reg_rst (
  input  RST,
  input  WE,
  input  D,
  output out_4,
  output out_5
);

  wire and_1_out, not_1_out, or_1_out;

  not not_1 (not_1_out, RST);
  or or_1 (or_1_out, RST, WE);
  and and_1 (and_1_out, not_1_out, D);
  my_d_reg my_d_reg_1 (.WE(or_1_out), .D(and_1_out), .Q(out_4), .Qn(out_5));
endmodule

module my_d_reg_loop (
  input  in_1,
  input  in_2
);

  wire my_d_reg_rst_1_out_4, not_1_out;

  my_d_reg_rst my_d_reg_rst_1 (.RST(in_1), .WE(in_2), .D(not_1_out), .out_4(my_d_reg_rst_1_out_4));  // open: out_5
  not not_1 (not_1_out, my_d_reg_rst_1_out_4);
endmodule

module my_dff_use (
  input  RST,
  input  CLK,
  input  D,
  input  EN,
  output Q
);

  wire my_d_reg_rst_1_out_4, not_1_out, not_2_out, or_1_out;

  not not_1 (not_1_out, EN);
  or or_1 (or_1_out, CLK, not_1_out);
  not not_2 (not_2_out, or_1_out);
  my_d_reg_rst my_d_reg_rst_1 (.RST(RST), .WE(not_2_out), .D(D), .out_4(my_d_reg_rst_1_out_4));  // open: out_5
  my_d_reg_rst my_d_reg_rst_2 (.RST(RST), .WE(or_1_out), .D(my_d_reg_rst_1_out_4), .out_4(Q));  // open: out_5
endmodule

module my_dff2 (
  input  in_1,
  input  in_2,
  output out_3,
  output out_4
);

  wire nand_1_out, nand_2_out, nand_3_out, nand_4_out;

  nand nand_1 (nand_1_out, nand_4_out, nand_2_out);
  nand nand_2 (nand_2_out, nand_1_out, in_1);
  nand nand_3 (nand_3_out, nand_2_out, in_1, nand_4_out);
  nand nand_4 (nand_4_out, nand_3_out, in_2);
  nand nand_5 (out_3, nand_2_out, out_4);
  nand nand_6 (out_4, out_3, nand_3_out);
endmodule

module my_dff_reset (
  input  RST,
  input  CLK,
  input  D,
  output Q
);

  wire my_d_reg_rst_1_out_4, not_1_out;

  not not_1 (not_1_out, CLK);
  my_d_reg_rst my_d_reg_rst_1 (.RST(RST), .WE(not_1_out), .D(D), .out_4(my_d_reg_rst_1_out_4));  // open: out_5
  my_d_reg_rst my_d_reg_rst_2 (.RST(RST), .WE(CLK), .D(my_d_reg_rst_1_out_4), .out_4(Q));  // open: out_5
endmodule

module my_dff_loop (
  input  in_1,
  input  in_2
);

  wire my_dff_reset_1_q, not_1_out;

  my_dff_reset my_dff_reset_1 (.RST(in_1), .CLK(in_2), .D(not_1_out), .Q(my_dff_reset_1_q));
  not not_1 (not_1_out, my_dff_reset_1_q);
endmodule

module my_dff_n (
  input  CLK,
  input  D,
  output out_3
);

  wire my_d_reg_1_q, not_1_out;

  not not_1 (not_1_out, CLK);
  my_d_reg my_d_reg_1 (.WE(CLK), .D(D), .Q(my_d_reg_1_q));  // open: Qn
  my_d_reg my_d_reg_2 (.WE(not_1_out), .D(my_d_reg_1_q), .Q(out_3));  // open: Qn
endmodule

module my_dff_en (
  input  EN,
  input  CLK,
  input  D,
  output out_4,
  output out_5
);

  wire not_1_out, or_1_out;

  not not_1 (not_1_out, EN);
  or or_1 (or_1_out, not_1_out, CLK);
  my_dff my_dff_1 (.CLK(or_1_out), .D(D), .Q(out_4), .Qn(out_5));
endmodule

module my_dff (
  input  CLK,
  input  D,
  output Q,
  output Qn
);

  wire my_d_reg_1_q, not_1_out;

  not not_1 (not_1_out, CLK);
  my_d_reg my_d_reg_1 (.WE(not_1_out), .D(D), .Q(my_d_reg_1_q));  // open: Qn
  my_d_reg my_d_reg_2 (.WE(CLK), .D(my_d_reg_1_q), .Q(Q), .Qn(Qn));
endmodule

module my_reg4 (
  input  RST,
  input  CLK,
  input  EN,
  input  [3:0] D,
  output [3:0] Q
);

  my_dff_use my_dff_use_1 (.RST(RST), .CLK(CLK), .D(D[0]), .EN(EN), .Q(Q[0]));
  my_dff_use my_dff_use_2 (.RST(RST), .CLK(CLK), .D(D[1]), .EN(EN), .Q(Q[1]));
  my_dff_use my_dff_use_3 (.RST(RST), .CLK(CLK), .D(D[2]), .EN(EN), .Q(Q[2]));
  my_dff_use my_dff_use_4 (.RST(RST), .CLK(CLK), .D(D[3]), .EN(EN), .Q(Q[3]));
endmodule

module my_cnt4 (
  input  [3:0] Max,
  input  RST,
  input  CLK,
  input  EN,
  output [3:0] CNT,
  output FULL
);

  wire [3:0] multiplexer_1_out, my_adder4_1_s, xnor_1_out;

  // Probe on multiplexer_1_out
  Hex_Digit_Display hex_digit_display_1 (.value(CNT));  // open: dp
  my_reg4 my_reg4_1 (.RST(RST), .CLK(CLK), .EN(EN), .D(multiplexer_1_out), .Q(CNT));
  // Probe on CNT
  Multiplexer #(.width(4)) multiplexer_1 (.in0(my_adder4_1_s), .in1(4'b0000), .out(multiplexer_1_out), .sel(FULL));
  my_adder4 my_adder4_1 (.A(4'b0000), .B(CNT), .Cin(1'b1), .S(my_adder4_1_s));  // open: Cout
  assign xnor_1_out = ~(Max ^ CNT);  // XNOR_Gate xnor_1, 4 bits wide
  and and_1 (FULL, xnor_1_out[0], xnor_1_out[1], xnor_1_out[2], xnor_1_out[3]);
endmodule

module my_reg8 (
  input  RST,
  input  CLK,
  input  EN,
  input  [7:0] D,
  output [7:0] Q
);

  my_reg4 my_reg4_1 (.RST(RST), .CLK(CLK), .EN(EN), .D(D[3:0]), .Q(Q[3:0]));
  my_reg4 my_reg4_2 (.RST(RST), .CLK(CLK), .EN(EN), .D(D[7:4]), .Q(Q[7:4]));
endmodule

module my_adder8 (
  input  Cin,
  input  [7:0] A,
  input  [7:0] B,
  output [7:0] S,
  output Cout
);

  wire my_adder4_1_cout;

  my_adder4 my_adder4_1 (.A(A[3:0]), .B(B[3:0]), .Cin(Cin), .S(S[3:0]), .Cout(my_adder4_1_cout));
  my_adder4 my_adder4_2 (.A(A[7:4]), .B(B[7:4]), .Cin(my_adder4_1_cout), .S(S[7:4]), .Cout(Cout));
endmodule

module my_sum_10 (
  input  RST,
  input  [3:0] in_2,
  output [7:0] out_3
);

  wire clock_1_out, nand_1_out;
  wire [3:0] my_cnt4_1_cnt, xnor_1_out;
  wire [7:0] my_adder8_1_s;

  Clock clock_1 (.out(clock_1_out));
  my_cnt4 my_cnt4_1 (.Max(4'b1111), .RST(RST), .CLK(clock_1_out), .EN(nand_1_out), .CNT(my_cnt4_1_cnt));  // open: FULL
  // Probe on my_cnt4_1_cnt
  // Probe on in_2
  // Probe on my_cnt4_1_cnt
  assign xnor_1_out = ~(my_cnt4_1_cnt ^ in_2);  // XNOR_Gate xnor_1, 4 bits wide
  nand nand_1 (nand_1_out, xnor_1_out[0], xnor_1_out[1], xnor_1_out[2], xnor_1_out[3]);
  my_adder8 my_adder8_1 (.Cin(1'b0), .A({4'b0000, my_cnt4_1_cnt}), .B(out_3), .S(my_adder8_1_s));  // open: Cout
  my_reg8 my_reg8_1 (.RST(RST), .CLK(clock_1_out), .EN(nand_1_out), .D(my_adder8_1_s), .Q(out_3));

  // Notes on the sheet:
  //   in_2: initial=0xb
endmodule

module my_clock (
  input  in_1
);

  wire and_1_out, and_2_out, clock_1_out, my_cnt4_1_full, my_cnt4_2_full, my_cnt4_3_full;
  wire [3:0] my_cnt4_1_cnt, my_cnt4_2_cnt, my_cnt4_3_cnt, my_cnt4_4_cnt;

  Clock clock_1 (.out(clock_1_out));
  my_cnt4 my_cnt4_1 (
    .Max(4'b1001), .RST(in_1), .CLK(clock_1_out), .EN(1'b1), .CNT(my_cnt4_1_cnt), .FULL(my_cnt4_1_full));
  my_cnt4 my_cnt4_2 (
    .Max(4'b0101), .RST(in_1), .CLK(clock_1_out), .EN(my_cnt4_1_full), .CNT(my_cnt4_2_cnt),
    .FULL(my_cnt4_2_full));
  and and_1 (and_1_out, my_cnt4_2_full, my_cnt4_1_full);
  my_cnt4 my_cnt4_3 (
    .Max(4'b1001), .RST(in_1), .CLK(clock_1_out), .EN(and_1_out), .CNT(my_cnt4_3_cnt), .FULL(my_cnt4_3_full));
  and and_2 (and_2_out, my_cnt4_3_full, my_cnt4_2_full, my_cnt4_1_full);
  my_cnt4 my_cnt4_4 (.Max(4'b0101), .RST(in_1), .CLK(clock_1_out), .EN(and_2_out), .CNT(my_cnt4_4_cnt));  // open: FULL
  Hex_Digit_Display hex_digit_display_1 (.value(my_cnt4_3_cnt));  // open: dp
  Hex_Digit_Display hex_digit_display_2 (.value(my_cnt4_4_cnt));  // open: dp
  Hex_Digit_Display hex_digit_display_3 (.value(my_cnt4_2_cnt));  // open: dp
  Hex_Digit_Display hex_digit_display_4 (.value(my_cnt4_1_cnt));  // open: dp
endmodule
