// Logisim project F5.circ as structural Verilog: 3 circuits, main circuit main
module main (
  input  in_1
);

  wire clock_1_out, comparator_1_eq, decoder_1_out0, decoder_1_out1, decoder_1_out2, decoder_1_out3,
       not_1_out, or_1_out, or_2_out;
  wire [1:0] multiplexer_2_out;
  wire [3:0] multiplexer_3_out, my_adder4_1_s, my_reg4_1_q;
  wire [7:0] multiplexer_1_out, my_adder8_1_s, my_ram_1_rdata1, my_ram_1_rdata2, my_reg8_1_q, my_rom_1_ins;

  Clock clock_1 (.out(clock_1_out));
  my_rom my_rom_1 (.PC(my_reg4_1_q), .ins(my_rom_1_ins));
  // Probe on my_rom_1_ins
  Decoder #(.enable("false"), .select(2)) decoder_1 (
    .out0(decoder_1_out0), .out1(decoder_1_out1), .out2(decoder_1_out2), .out3(decoder_1_out3),
    .sel(my_rom_1_ins[7:6]));
  or or_1 (or_1_out, decoder_1_out0, decoder_1_out2);
  // Probe on multiplexer_3_out
  Multiplexer #(.width(8)) multiplexer_1 (
    .in0(my_adder8_1_s), .in1({4'b0000, my_rom_1_ins[3:0]}), .out(multiplexer_1_out), .sel(decoder_1_out2));
  // Probe on multiplexer_1_out
  Multiplexer #(.width(2)) multiplexer_2 (
    .in0(my_rom_1_ins[3:2]), .in1(2'b00), .out(multiplexer_2_out), .sel(decoder_1_out3));
  // Probe on my_rom_1_ins[5:4]
  my_reg4 my_reg4_1 (.RST(in_1), .CLK(clock_1_out), .EN(1'b1), .D(multiplexer_3_out), .Q(my_reg4_1_q));
  Multiplexer #(.width(4)) multiplexer_3 (
    .in0(my_rom_1_ins[5:2]), .in1(my_adder4_1_s), .out(multiplexer_3_out), .sel(or_2_out));
  my_reg8 my_reg8_1 (.RST(in_1), .CLK(clock_1_out), .EN(decoder_1_out1), .D(my_ram_1_rdata2), .Q(my_reg8_1_q));
  // Probe on my_reg4_1_q
  Hex_Digit_Display hex_digit_display_1 (.value(my_reg8_1_q[7:4]));  // open: dp
  Hex_Digit_Display hex_digit_display_2 (.value(my_reg8_1_q[3:0]));  // open: dp
  my_ram my_ram_1 (
    .clk(clock_1_out), .wdata(multiplexer_1_out), .raddr1(multiplexer_2_out), .wen(or_1_out),
    .raddr2(my_rom_1_ins[1:0]), .waddr(my_rom_1_ins[5:4]), .rdata1(my_ram_1_rdata1), .rdata2(my_ram_1_rdata2));
  not not_1 (not_1_out, decoder_1_out3);
  my_adder4 my_adder4_1 (.B(my_reg4_1_q), .Cin(1'b1), .S(my_adder4_1_s));  // open: A, Cout
  Comparator comparator_1 (.a(my_ram_1_rdata1), .b(my_ram_1_rdata2), .eq(comparator_1_eq));  // open: gt, lt
  my_adder8 my_adder8_1 (.A(my_ram_1_rdata1), .B(my_ram_1_rdata2), .S(my_adder8_1_s));  // open: Cin, Cout
  or or_2 (or_2_out, comparator_1_eq, not_1_out);

  // Notes on the sheet:
  //   out: 01|xxxx|rs2
endmodule

module my_rom (
  input  [3:0] PC,
  output [7:0] ins
);

  Multiplexer #(.select(4), .width(8)) multiplexer_1 (
    .in0(8'h8b), .in1(8'h91), .in2(8'ha0), .in3(8'hb2), .in4(8'h26), .in5(8'h17), .in6(8'hd1), .in7(8'h42),
    .in8(8'he3), .in9({8{1'b1}}), .in10({8{1'b1}}), .in11({8{1'b1}}), .in12({8{1'b1}}), .in13({8{1'b1}}),
    .in14({8{1'b1}}), .in15({8{1'b1}}), .out(ins), .sel(PC));
endmodule

module my_ram (
  input  clk,
  input  [7:0] wdata,
  input  [1:0] raddr1,
  input  wen,
  input  [1:0] raddr2,
  input  [1:0] waddr,
  output [7:0] rdata1,
  output [7:0] rdata2
);

  wire and_1_out, and_2_out, and_3_out, and_4_out, decoder_1_out0, decoder_1_out1, decoder_1_out2,
       decoder_1_out3;
  wire [7:0] register_1_q, register_2_q, register_3_q, register_4_q;

  Decoder #(.enable("false"), .select(2)) decoder_1 (
    .out0(decoder_1_out0), .out1(decoder_1_out1), .out2(decoder_1_out2), .out3(decoder_1_out3), .sel(waddr));
  and and_1 (and_1_out, wen, decoder_1_out0);
  and and_2 (and_2_out, wen, decoder_1_out1);
  and and_3 (and_3_out, wen, decoder_1_out2);
  and and_4 (and_4_out, wen, decoder_1_out3);
  Register register_1 (.D(wdata), .en(and_1_out), .clk(clk), .Q(register_1_q));  // open: clr
  Register register_2 (.D(wdata), .en(and_2_out), .clk(clk), .Q(register_2_q));  // open: clr
  Register register_3 (.D(wdata), .en(and_3_out), .clk(clk), .Q(register_3_q));  // open: clr
  Register register_4 (.D(wdata), .en(and_4_out), .clk(clk), .Q(register_4_q));  // open: clr
  Multiplexer #(.select(2), .width(8)) multiplexer_1 (
    .in0(register_1_q), .in1(register_2_q), .in2(register_3_q), .in3(register_4_q), .out(rdata1), .sel(raddr1));
  Multiplexer #(.select(2), .width(8)) multiplexer_2 (
    .in0(register_1_q), .in1(register_2_q), .in2(register_3_q), .in3(register_4_q), .out(rdata2), .sel(raddr2));
endmodule
