// Logisim project F6.circ as structural Verilog: 3 circuits, main circuit main
module main (
  input  in_1
);

  wire and_1_out, and_2_out, and_3_out, clock_1_out, comparator_1_lt, comparator_2_gt, comparator_3_eq,
       comparator_4_eq, comparator_5_eq, comparator_6_eq, comparator_7_eq, comparator_8_eq, comparator_9_eq,
       comparator_10_eq, or_1_out, or_2_out;
  wire [1:0] adder_2_out;
  wire [3:0] decoder_1_out0, multiplexer_7_out;
  wire [4:0] multiplexer_2_out;
  wire [7:0] gprs_1_rdata2, multiplexer_10_out, rgb_video_1_p2, rgb_video_1_p3;
  wire [11:0] rom_1_data;
  wire [13:0] adder_2_out_2;
  wire [21:0] adder_1_out, multiplexer_1_out, register_1_q;
  wire [23:0] rgb_video_1_p4;
  wire [31:0] bit_extender_1_out, bit_extender_2_out, gprs_1_rdata1, multiplexer_3_out, multiplexer_4_out,
       multiplexer_5_out, multiplexer_6_out, multiplexer_8_out, multiplexer_9_out, multiplexer_11_out,
       ram_1_dout;
  wire [31:12] rom_1_data_2;
  wire [63:0] counter_1_q;

  Clock clock_1 (.out(clock_1_out));
  // Probe on multiplexer_1_out
  Register #(.width(22)) register_1 (.D(multiplexer_1_out), .en(1'b1), .clk(clock_1_out), .Q(register_1_q), .clr(in_1));
  Counter #(.max('hffffffffffffffff), .width(64)) counter_1 (
    .clr(in_1), .load(1'b0), .up(1'b1), .clk(clock_1_out), .Q(counter_1_q));  // open: count, D, carry
  Multiplexer #(.width(22)) multiplexer_1 (
    .in0(adder_1_out), .in1({adder_2_out_2[3:0], rgb_video_1_p3, rgb_video_1_p2, adder_2_out[1], 1'b0}),
    .out(multiplexer_1_out), .sel(comparator_8_eq));
  ROM #(.addrWidth(20), .dataWidth(32)) rom_1 (.addr(register_1_q[21:2]), .data({rom_1_data_2, rom_1_data}));
  Adder #(.width(22)) adder_1 (.a(register_1_q), .b(22'h4), .out(adder_1_out), .cin(1'b0));  // open: cout
  // Probe on counter_1_q
  // Probe on rom_1_data_2[14:12]
  // Probe on rom_1_data[11:7]
  // Probe on rom_1_data_2[19:15]
  // Probe on rom_1_data_2[24:20]
  // Probe on adder_2_out_2
  Comparator #(.width(14)) comparator_1 (.a(adder_2_out_2), .b(14'h802), .lt(comparator_1_lt));  // open: gt, eq
  Comparator #(.width(14)) comparator_2 (.a(adder_2_out_2), .b(14'h799), .gt(comparator_2_gt));  // open: eq, lt
  Comparator #(.width(7)) comparator_3 (.a(rom_1_data[6:0]), .b(7'b0110011), .eq(comparator_3_eq));  // open: gt, lt
  Comparator #(.width(7)) comparator_4 (.a(rom_1_data[6:0]), .b(7'b0010011), .eq(comparator_4_eq));  // open: gt, lt
  Comparator #(.width(7)) comparator_5 (.a(rom_1_data[6:0]), .b(7'b0110111), .eq(comparator_5_eq));  // open: gt, lt
  Comparator #(.width(7)) comparator_6 (.a(rom_1_data[6:0]), .b(7'b0000011), .eq(comparator_6_eq));  // open: gt, lt
  Comparator #(.width(7)) comparator_7 (.a(rom_1_data[6:0]), .b(7'b0100011), .eq(comparator_7_eq));  // open: gt, lt
  Comparator #(.width(7)) comparator_8 (.a(rom_1_data[6:0]), .b(7'b1100111), .eq(comparator_8_eq));  // open: gt, lt
  Comparator #(.width(3)) comparator_9 (.a(rom_1_data_2[14:12]), .b(3'b010), .eq(comparator_9_eq));  // open: gt, lt
  Comparator #(.width(3)) comparator_10 (.a(rom_1_data_2[14:12]), .b(3'b100), .eq(comparator_10_eq));  // open: gt, lt
  // RGB_Video #(.height(256), .width(256)) rgb_video_1: pin names not known; wires that end beside it: clock_1_out, rgb_video_1_p2, rgb_video_1_p3, rgb_video_1_p4
  and and_1 (and_1_out, comparator_1_lt, comparator_2_gt);
  and and_2 (and_2_out, comparator_7_eq, ~and_1_out);  // AND_Gate
  or or_1 (or_1_out, comparator_3_eq, comparator_4_eq, comparator_8_eq, comparator_5_eq, comparator_6_eq);
  or or_2 (or_2_out, comparator_9_eq, comparator_10_eq);
  and and_3 (and_3_out, comparator_6_eq, ~and_1_out);  // AND_Gate
  // Probe on multiplexer_4_out
  // Probe on {gprs_1_rdata2, rgb_video_1_p4}
  Multiplexer #(.width(5)) multiplexer_2 (
    .in0(rom_1_data_2[24:20]), .in1(rom_1_data[11:7]), .out(multiplexer_2_out), .sel(comparator_7_eq));
  // Probe on multiplexer_3_out
  Multiplexer #(.width(32)) multiplexer_3 (
    .in0({rgb_video_1_p4[7:0], rgb_video_1_p4[7:0], rgb_video_1_p4[7:0], rgb_video_1_p4[7:0]}),
    .in1({gprs_1_rdata2, rgb_video_1_p4}), .out(multiplexer_3_out), .sel(or_2_out));
  GPRs gprs_1 (
    .CLK(clock_1_out), .RST(in_1), .EN(or_1_out), .WDATA(multiplexer_4_out), .WADDR(rom_1_data[11:7]),
    .RADDR1(rom_1_data_2[19:15]), .RADDR2(rom_1_data_2[24:20]), .RDATA1(gprs_1_rdata1),
    .RDATA2({gprs_1_rdata2, rgb_video_1_p4}));
  RAM #(.addrWidth(20), .asyncread("true"), .byteenables("byteEnables"), .dataWidth(32), .\type ("nonvolatile")) ram_1 (
    .addr({adder_2_out_2[3:0], rgb_video_1_p3, rgb_video_1_p2}), .we(and_2_out), .oe(and_3_out),
    .clk(clock_1_out), .din(multiplexer_3_out), .dout(ram_1_dout), .be3(multiplexer_7_out[3]),
    .be2(multiplexer_7_out[2]), .be1(multiplexer_7_out[1]), .be0(multiplexer_7_out[0]));
  assign bit_extender_1_out = {{20{rom_1_data_2[31]}}, {rom_1_data_2[31:25], multiplexer_2_out}};  // Bit_Extender bit_extender_1
  Multiplexer #(.width(32)) multiplexer_4 (
    .in0(multiplexer_6_out), .in1(multiplexer_11_out), .out(multiplexer_4_out), .sel(comparator_6_eq));
  // Probe on {rom_1_data_2, {12{1'b0}}}
  // Probe on bit_extender_1_out
  // Probe on gprs_1_rdata1
  // Probe on {gprs_1_rdata2, rgb_video_1_p4}
  // Probe on {adder_2_out_2[3:0], rgb_video_1_p3, rgb_video_1_p2}
  Multiplexer #(.width(32)) multiplexer_5 (
    .in0(bit_extender_1_out), .in1({rom_1_data_2, {12{1'b0}}}), .out(multiplexer_5_out), .sel(comparator_5_eq));
  Multiplexer #(.width(32)) multiplexer_6 (
    .in0({adder_2_out_2, rgb_video_1_p3, rgb_video_1_p2, adder_2_out}), .in1({{10{1'b0}}, adder_1_out}),
    .out(multiplexer_6_out), .sel(comparator_8_eq));
  Multiplexer #(.width(4)) multiplexer_7 (.in0(decoder_1_out0), .in1(4'b1111), .out(multiplexer_7_out), .sel(or_2_out));
  // Probe on ram_1_dout
  Multiplexer #(.width(32)) multiplexer_8 (
    .in0(multiplexer_5_out), .in1({gprs_1_rdata2, rgb_video_1_p4}), .out(multiplexer_8_out),
    .sel(comparator_3_eq));
  // Probe on multiplexer_8_out
  // Probe on multiplexer_9_out
  Multiplexer #(.width(32)) multiplexer_9 (
    .in0(gprs_1_rdata1), .in1({32{1'b0}}), .out(multiplexer_9_out), .sel(comparator_5_eq));
  Multiplexer #(.select(2), .width(8)) multiplexer_10 (
    .in0(ram_1_dout[7:0]), .in1(ram_1_dout[15:8]), .in2(ram_1_dout[23:16]), .in3(ram_1_dout[31:24]),
    .out(multiplexer_10_out), .sel(adder_2_out));
  Adder #(.width(32)) adder_2 (
    .a(multiplexer_8_out), .b(multiplexer_9_out),
    .out({adder_2_out_2, rgb_video_1_p3, rgb_video_1_p2, adder_2_out}));  // open: cin, cout
  // Probe on {adder_2_out_2, rgb_video_1_p3, rgb_video_1_p2, adder_2_out}
  // Probe on {adder_2_out_2, rgb_video_1_p3, rgb_video_1_p2, adder_2_out}
  Decoder #(.enable("false"), .select(2)) decoder_1 (
    .out0(decoder_1_out0[0]), .out1(decoder_1_out0[1]), .out2(decoder_1_out0[2]), .out3(decoder_1_out0[3]),
    .sel(adder_2_out));
  assign bit_extender_2_out = {{24{1'b0}}, multiplexer_10_out};  // Bit_Extender bit_extender_2
  Multiplexer #(.width(32)) multiplexer_11 (
    .in0(ram_1_dout), .in1(bit_extender_2_out), .out(multiplexer_11_out), .sel(comparator_10_eq));

  // Notes on the sheet:
  //   contents of rom_1 (hex, n*v repeats v):
  //   413 93137 10113 10b7 dbc08093 80e7 fe012823 fea10923 fea12423 fe914203 fe4109a3 ff012783 f787b3
  //   f787b3 4b6b7 af868693 fdc10113 d787b3 10000713 f12423 10593 100793 b00513 2112023 12023 12223 e12623
  //   e12823 f10a23 10b7 a8408093 80e7 2012083 2410113 8067 ff410113 112423 10b7 a7c08093 80e7 513 1800093
  //   80e7 812083 513 c10113 8067 852583 feb12823 fe812e23 3437 80840413 ff014183 3401b3 1c183 ff114203
  //   440233 24203 4181b3 ff214203 440233 24203 4181b3 ff314203 440233 24203 4181b3 3237 80020213 320233
  //   24203 ffc12403 420233 420233 410233 11b7 86418193 fe312823 14800193 fe312623 fec22203 20067 1052703
  //   52683 452783 fe810113 e12423 112a23 812823 912623 fed12823 fef12623 13737 a0070713 fe012223 ff314203
  //   fe4102a3 fef14203 fe410223 fe412203 470233 24203 fe4105a3 ff214203 fe4102a3 fee14203 fe410223
  //   fe412203 470233 24203 fe410523 ff114203 fe4102a3 fed14203 fe410223 fe412203 470233 24203 fe4104a3
  //   ff014203 fe4102a3 fec14203 fe410223 fe412203 470233 24203 fe410423 fe812703 c52603 fee12823 fe812e23
  //   3437 80840413 ff014183 3401b3 1c183 ff114203 440233 24203 4181b3 ff214203 440233 24203 4181b3
  //   ff314203 440233 24203 4181b3 3237 80020213 320233 24203 ffc12403 420233 420233 410233 66800193
  //   fe312823 28800193 fe312623 fec22203 20067 c68733 10000513 fe812e23 fe912c23 fee12823 50413 ff012483
  //   fe812423 feb14183 3181b3 fe312423 fe914183 3181b3 fe912423 feb14203 420233 fe412423 fe914203 4181b3
  //   3181b3 fe312a23 fe912423 33237 90020213 feb14183 4181b3 1c183 fe3103a3 fea14183 4181b3 1c183
  //   fe310323 fe914183 4181b3 1c183 fe3102a3 fe814183 4181b3 1c183 fe310223 ff412183 fe412203 440233
  //   120213 fe412423 feb14203 420233 fe412423 fe914203 4181b3 3237 90820213 320233 ff812483 ffc12403
  //   24203 420233 420233 410233 11b7 86818193 fe312823 39000193 fe312623 fec22203 20067 812703 10000513
  //   e78733 fe812e23 fe912c23 fee12823 50413 ff012483 fe812423 feb14183 3181b3 fe312423 fe914183 3181b3
  //   fe912423 feb14203 420233 fe412423 fe914203 4181b3 3181b3 fe312a23 fe912423 33237 90020213 feb14183
  //   4181b3 1c183 fe3103a3 fea14183 4181b3 1c183 fe310323 fe914183 4181b3 1c183 fe3102a3 fe814183 4181b3
  //   1c183 fe310223 ff412183 fe412203 440233 120213 fe412423 feb14203 420233 fe412423 fe914203 4181b3
  //   3237 90820213 320233 ff812483 ffc12403 24203 420233 420233 410233 11b7 86818193 fe312823 49c00193
  //   fe312623 fec22203 20067 8*f787b3 d787b3 f787b3 f787b3 20000437 f40433 812783 c60633 c60633 fef12423
  //   feb14183 3181b3 fe312423 fe914183 fff78213 fe412423 feb14203 420233 fe412423 fe914203 4181b3 3237
  //   91820213 418233 24203 420233 420233 410233 65400193 fe312823 54000193 fe312623 fec22203 20067 493
  //   40513 b12223 c12023 10b7 de008093 80e7 12603 412583 812783 148493 40040413 c585b3 fef12823 fe912623
  //   fe812e23 fe912c23 2437 70040413 ff014183 340233 100193 320023 fec14183 3401b3 18023 24183 ff114483
  //   940233 100493 920023 fed14483 9404b3 48023 24483 9181b3 ff214483 940233 100493 920023 fee14483
  //   9404b3 48023 24483 9181b3 ff314483 940233 100493 920023 fef14483 9404b3 48023 24483 9181b3 3237
  //   80020213 320233 24203 ff812483 ffc12403 420233 420233 410233 65400193 fe312823 54400193 fe312623
  //   fec22203 20067 1412083 1012403 c12483 1810113 8067 10000713 fec12823 fee12623 fe812e23 fe912c23 2437
  //   70040413 ff014183 340233 100193 320023 fec14183 3401b3 18023 24183 ff114483 940233 100493 920023
  //   fed14483 9404b3 48023 24483 9181b3 ff214483 940233 100493 920023 fee14483 9404b3 48023 24483 9181b3
  //   ff314483 940233 100493 920023 fef14483 9404b3 48023 24483 9181b3 3237 80020213 320233 24203 ff812483
  //   ffc12403 420233 420233 410233 74c00193 fe312823 28800193 fe312623 fec22203 20067 812703 fee12823
  //   fec12623 fe812e23 fe912c23 2437 70040413 ff014183 340233 100193 320023 fec14183 3401b3 18023 24183
  //   ff114483 940233 100493 920023 fed14483 9404b3 48023 24483 9181b3 ff214483 940233 100493 920023
  //   fee14483 9404b3 48023 24483 9181b3 ff314483 940233 100493 920023 fef14483 9404b3 48023 24483 9181b3
  //   3237 80020213 320233 24203 ff812483 ffc12403 420233 420233 410233 11b7 83418193 fe312823 39000193
  //   fe312623 fec22203 20067 1012403 1412083 c12483 40637 20000537 1810113 1237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
endmodule

module GPR (
  input  CLK,
  input  RST,
  input  EN,
  input  WSEL,
  input  [31:0] WDATA,
  input  RSEL1,
  input  RSEL2,
  output [31:0] RDATA1,
  output [31:0] RDATA2,
  output [31:0] DATA
);

  wire and_1_out;

  and and_1 (and_1_out, EN, WSEL);
  Register #(.width(32)) register_1 (.D(WDATA), .en(and_1_out), .clk(CLK), .Q(DATA), .clr(RST));
  assign RDATA1 = RSEL1 ? DATA : 32'bz;  // Controlled_Buffer controlled_buffer_1
  assign RDATA2 = RSEL2 ? DATA : 32'bz;  // Controlled_Buffer controlled_buffer_2
endmodule

module GPRs (
  input  CLK,
  input  RST,
  input  EN,
  input  [31:0] WDATA,
  input  [4:0] WADDR,
  input  [4:0] RADDR1,
  input  [4:0] RADDR2,
  output [31:0] RDATA1,
  output [31:0] RDATA2
);

  wire decoder_1_out0, decoder_1_out1, decoder_1_out2, decoder_1_out3, decoder_1_out4, decoder_1_out5,
       decoder_1_out6, decoder_1_out7, decoder_1_out8, decoder_1_out9, decoder_1_out10, decoder_1_out11,
       decoder_1_out12, decoder_1_out13, decoder_1_out14, decoder_1_out15, decoder_2_out0, decoder_2_out1,
       decoder_2_out2, decoder_2_out3, decoder_2_out4, decoder_2_out5, decoder_2_out6, decoder_2_out7,
       decoder_2_out8, decoder_2_out9, decoder_2_out10, decoder_2_out11, decoder_2_out12, decoder_2_out13,
       decoder_2_out14, decoder_2_out15, decoder_3_out0, decoder_3_out1, decoder_3_out2, decoder_3_out3,
       decoder_3_out4, decoder_3_out5, decoder_3_out6, decoder_3_out7, decoder_3_out8, decoder_3_out9,
       decoder_3_out10, decoder_3_out11, decoder_3_out12, decoder_3_out13, decoder_3_out14, decoder_3_out15;
  wire [31:0] gpr_1_data, gpr_2_data, gpr_3_data, gpr_4_data, gpr_5_data, gpr_6_data, gpr_7_data, gpr_8_data,
       gpr_9_data, gpr_10_data, gpr_11_data, gpr_12_data, gpr_13_data, gpr_14_data, gpr_15_data, gpr_16_data;

  Decoder #(.select(4)) decoder_1 (
    .out0(decoder_1_out0), .out1(decoder_1_out1), .out2(decoder_1_out2), .out3(decoder_1_out3),
    .out4(decoder_1_out4), .out5(decoder_1_out5), .out6(decoder_1_out6), .out7(decoder_1_out7),
    .out8(decoder_1_out8), .out9(decoder_1_out9), .out10(decoder_1_out10), .out11(decoder_1_out11),
    .out12(decoder_1_out12), .out13(decoder_1_out13), .out14(decoder_1_out14), .out15(decoder_1_out15),
    .sel(WADDR[3:0]));  // open: en
  Decoder #(.select(4)) decoder_2 (
    .out0(decoder_2_out0), .out1(decoder_2_out1), .out2(decoder_2_out2), .out3(decoder_2_out3),
    .out4(decoder_2_out4), .out5(decoder_2_out5), .out6(decoder_2_out6), .out7(decoder_2_out7),
    .out8(decoder_2_out8), .out9(decoder_2_out9), .out10(decoder_2_out10), .out11(decoder_2_out11),
    .out12(decoder_2_out12), .out13(decoder_2_out13), .out14(decoder_2_out14), .out15(decoder_2_out15),
    .sel(RADDR1[3:0]));  // open: en
  Decoder #(.select(4)) decoder_3 (
    .out0(decoder_3_out0), .out1(decoder_3_out1), .out2(decoder_3_out2), .out3(decoder_3_out3),
    .out4(decoder_3_out4), .out5(decoder_3_out5), .out6(decoder_3_out6), .out7(decoder_3_out7),
    .out8(decoder_3_out8), .out9(decoder_3_out9), .out10(decoder_3_out10), .out11(decoder_3_out11),
    .out12(decoder_3_out12), .out13(decoder_3_out13), .out14(decoder_3_out14), .out15(decoder_3_out15),
    .sel(RADDR2[3:0]));  // open: en
  GPR gpr_1 (
    .CLK(CLK), .RST(RST), .EN(EN), .WSEL(decoder_1_out12), .WDATA(WDATA), .RSEL1(decoder_2_out12),
    .RSEL2(decoder_3_out12), .RDATA1(RDATA1), .RDATA2(RDATA2), .DATA(gpr_1_data));
  // Probe on gpr_1_data
  GPR gpr_2 (
    .CLK(CLK), .RST(RST), .EN(EN), .WSEL(decoder_1_out13), .WDATA(WDATA), .RSEL1(decoder_2_out13),
    .RSEL2(decoder_3_out13), .RDATA1(RDATA1), .RDATA2(RDATA2), .DATA(gpr_2_data));
  // Probe on gpr_2_data
  GPR gpr_3 (
    .CLK(CLK), .RST(RST), .EN(EN), .WSEL(decoder_1_out14), .WDATA(WDATA), .RSEL1(decoder_2_out14),
    .RSEL2(decoder_3_out14), .RDATA1(RDATA1), .RDATA2(RDATA2), .DATA(gpr_3_data));
  // Probe on gpr_3_data
  GPR gpr_4 (
    .CLK(CLK), .RST(RST), .EN(EN), .WSEL(decoder_1_out15), .WDATA(WDATA), .RSEL1(decoder_2_out15),
    .RSEL2(decoder_3_out15), .RDATA1(RDATA1), .RDATA2(RDATA2), .DATA(gpr_4_data));
  // Probe on gpr_4_data
  GPR gpr_5 (
    .CLK(CLK), .RST(RST), .EN(EN), .WSEL(decoder_1_out8), .WDATA(WDATA), .RSEL1(decoder_2_out8),
    .RSEL2(decoder_3_out8), .RDATA1(RDATA1), .RDATA2(RDATA2), .DATA(gpr_5_data));
  // Probe on gpr_5_data
  GPR gpr_6 (
    .CLK(CLK), .RST(RST), .EN(EN), .WSEL(decoder_1_out9), .WDATA(WDATA), .RSEL1(decoder_2_out9),
    .RSEL2(decoder_3_out9), .RDATA1(RDATA1), .RDATA2(RDATA2), .DATA(gpr_6_data));
  // Probe on gpr_6_data
  GPR gpr_7 (
    .CLK(CLK), .RST(RST), .EN(EN), .WSEL(decoder_1_out10), .WDATA(WDATA), .RSEL1(decoder_2_out10),
    .RSEL2(decoder_3_out10), .RDATA1(RDATA1), .RDATA2(RDATA2), .DATA(gpr_7_data));
  // Probe on gpr_7_data
  GPR gpr_8 (
    .CLK(CLK), .RST(RST), .EN(EN), .WSEL(decoder_1_out11), .WDATA(WDATA), .RSEL1(decoder_2_out11),
    .RSEL2(decoder_3_out11), .RDATA1(RDATA1), .RDATA2(RDATA2), .DATA(gpr_8_data));
  // Probe on gpr_8_data
  GPR gpr_9 (
    .CLK(CLK), .RST(RST), .EN(EN), .WSEL(decoder_1_out4), .WDATA(WDATA), .RSEL1(decoder_2_out4),
    .RSEL2(decoder_3_out4), .RDATA1(RDATA1), .RDATA2(RDATA2), .DATA(gpr_9_data));
  // Probe on gpr_9_data
  GPR gpr_10 (
    .CLK(CLK), .RST(RST), .EN(EN), .WSEL(decoder_1_out5), .WDATA(WDATA), .RSEL1(decoder_2_out5),
    .RSEL2(decoder_3_out5), .RDATA1(RDATA1), .RDATA2(RDATA2), .DATA(gpr_10_data));
  // Probe on gpr_10_data
  GPR gpr_11 (
    .CLK(CLK), .RST(RST), .EN(EN), .WSEL(decoder_1_out6), .WDATA(WDATA), .RSEL1(decoder_2_out6),
    .RSEL2(decoder_3_out6), .RDATA1(RDATA1), .RDATA2(RDATA2), .DATA(gpr_11_data));
  // Probe on gpr_11_data
  GPR gpr_12 (
    .CLK(CLK), .RST(RST), .EN(EN), .WSEL(decoder_1_out7), .WDATA(WDATA), .RSEL1(decoder_2_out7),
    .RSEL2(decoder_3_out7), .RDATA1(RDATA1), .RDATA2(RDATA2), .DATA(gpr_12_data));
  // Probe on gpr_12_data
  GPR gpr_13 (
    .CLK(CLK), .RST(RST), .EN(1'b0), .WSEL(decoder_1_out0), .WDATA(WDATA), .RSEL1(decoder_2_out0),
    .RSEL2(decoder_3_out0), .RDATA1(RDATA1), .RDATA2(RDATA2), .DATA(gpr_13_data));
  // Probe on gpr_13_data
  GPR gpr_14 (
    .CLK(CLK), .RST(RST), .EN(EN), .WSEL(decoder_1_out1), .WDATA(WDATA), .RSEL1(decoder_2_out1),
    .RSEL2(decoder_3_out1), .RDATA1(RDATA1), .RDATA2(RDATA2), .DATA(gpr_14_data));
  // Probe on gpr_14_data
  GPR gpr_15 (
    .CLK(CLK), .RST(RST), .EN(EN), .WSEL(decoder_1_out2), .WDATA(WDATA), .RSEL1(decoder_2_out2),
    .RSEL2(decoder_3_out2), .RDATA1(RDATA1), .RDATA2(RDATA2), .DATA(gpr_15_data));
  // Probe on gpr_15_data
  GPR gpr_16 (
    .CLK(CLK), .RST(RST), .EN(EN), .WSEL(decoder_1_out3), .WDATA(WDATA), .RSEL1(decoder_2_out3),
    .RSEL2(decoder_3_out3), .RDATA1(RDATA1), .RDATA2(RDATA2), .DATA(gpr_16_data));
  // Probe on gpr_16_data
endmodule
